// Logisim project processor.circ as structural Verilog
module program_counter (
  input  enable,
  input  clock,
  input  reset,
  output [7:0] address
);

  wire [7:0] adder_1_out;

  Register register_1 (.D(adder_1_out), .en(enable), .clk(clock), .Q(address), .clr(reset));
  Adder adder_1 (.a(8'h1), .b(address), .out(adder_1_out));  // open: cin, cout
endmodule

module monocycle_processor (
  input  reset,
  input  in_2,
  output [7:0] out_3,
  output [31:0] out_4
);

  wire clock_1_out;

  Clock clock_1 (.out(clock_1_out));
  ROM #(.dataWidth(32)) rom_1 (.addr(out_3), .data(out_4));
  program_counter program_counter_1 (.enable(in_2), .clock(clock_1_out), .reset(reset), .address(out_3));
  register_file register_file_1 ();  // open: write_data, write_enable, write_register, read_rg_2, read_rg_1, clock, read_data_2, read_data_1

  // Notes on the sheet:
  //   contents of rom_1 (hex, n*v repeats v):
  //   8*0 4
endmodule

module register_file (
  input  [31:0] write_data,
  input  write_enable,
  input  [4:0] write_register,
  input  [4:0] read_rg_2,
  input  [4:0] read_rg_1,
  input  clock,
  output [31:0] read_data_2,
  output [31:0] read_data_1
);

  wire demultiplexer_1_out0, demultiplexer_1_out1, demultiplexer_1_out2, demultiplexer_1_out3,
       demultiplexer_1_out4, demultiplexer_1_out5, demultiplexer_1_out6, demultiplexer_1_out7,
       demultiplexer_1_out8, demultiplexer_1_out9, demultiplexer_1_out10, demultiplexer_1_out11,
       demultiplexer_1_out12, demultiplexer_1_out13, demultiplexer_1_out14, demultiplexer_1_out15,
       demultiplexer_1_out16, demultiplexer_1_out17, demultiplexer_1_out18, demultiplexer_1_out19,
       demultiplexer_1_out20, demultiplexer_1_out21, demultiplexer_1_out22, demultiplexer_1_out23,
       demultiplexer_1_out24, demultiplexer_1_out25, demultiplexer_1_out26, demultiplexer_1_out27,
       demultiplexer_1_out28, demultiplexer_1_out29, demultiplexer_1_out30, demultiplexer_1_out31;
  wire [31:0] register_1_q, register_2_q, register_3_q, register_4_q, register_5_q, register_6_q,
       register_7_q, register_8_q, register_9_q, register_10_q, register_11_q, register_12_q, register_13_q,
       register_14_q, register_15_q, register_16_q, register_17_q, register_18_q, register_19_q,
       register_20_q, register_21_q, register_22_q, register_23_q, register_24_q, register_25_q,
       register_26_q, register_27_q, register_28_q, register_29_q, register_30_q, register_31_q,
       register_32_q;

  Demultiplexer #(.select(5)) demultiplexer_1 (
    .out0(demultiplexer_1_out0), .out1(demultiplexer_1_out1), .out2(demultiplexer_1_out2),
    .out3(demultiplexer_1_out3), .out4(demultiplexer_1_out4), .out5(demultiplexer_1_out5),
    .out6(demultiplexer_1_out6), .out7(demultiplexer_1_out7), .out8(demultiplexer_1_out8),
    .out9(demultiplexer_1_out9), .out10(demultiplexer_1_out10), .out11(demultiplexer_1_out11),
    .out12(demultiplexer_1_out12), .out13(demultiplexer_1_out13), .out14(demultiplexer_1_out14),
    .out15(demultiplexer_1_out15), .out16(demultiplexer_1_out16), .out17(demultiplexer_1_out17),
    .out18(demultiplexer_1_out18), .out19(demultiplexer_1_out19), .out20(demultiplexer_1_out20),
    .out21(demultiplexer_1_out21), .out22(demultiplexer_1_out22), .out23(demultiplexer_1_out23),
    .out24(demultiplexer_1_out24), .out25(demultiplexer_1_out25), .out26(demultiplexer_1_out26),
    .out27(demultiplexer_1_out27), .out28(demultiplexer_1_out28), .out29(demultiplexer_1_out29),
    .out30(demultiplexer_1_out30), .out31(demultiplexer_1_out31), .in(write_enable), .sel(write_register));
  Register #(.width(32)) register_1 (
    .D(write_data), .en(demultiplexer_1_out0), .clk(clock), .Q(register_1_q));  // open: clr
  Register #(.width(32)) register_2 (
    .D(write_data), .en(demultiplexer_1_out1), .clk(clock), .Q(register_2_q));  // open: clr
  Register #(.width(32)) register_3 (
    .D(write_data), .en(demultiplexer_1_out2), .clk(clock), .Q(register_3_q));  // open: clr
  Register #(.width(32)) register_4 (
    .D(write_data), .en(demultiplexer_1_out3), .clk(clock), .Q(register_4_q));  // open: clr
  Register #(.width(32)) register_5 (
    .D(write_data), .en(demultiplexer_1_out4), .clk(clock), .Q(register_5_q));  // open: clr
  Register #(.width(32)) register_6 (
    .D(write_data), .en(demultiplexer_1_out5), .clk(clock), .Q(register_6_q));  // open: clr
  Register #(.width(32)) register_7 (
    .D(write_data), .en(demultiplexer_1_out6), .clk(clock), .Q(register_7_q));  // open: clr
  Register #(.width(32)) register_8 (
    .D(write_data), .en(demultiplexer_1_out7), .clk(clock), .Q(register_8_q));  // open: clr
  Register #(.width(32)) register_9 (
    .D(write_data), .en(demultiplexer_1_out8), .clk(clock), .Q(register_9_q));  // open: clr
  Register #(.width(32)) register_10 (
    .D(write_data), .en(demultiplexer_1_out9), .clk(clock), .Q(register_10_q));  // open: clr
  Register #(.width(32)) register_11 (
    .D(write_data), .en(demultiplexer_1_out10), .clk(clock), .Q(register_11_q));  // open: clr
  Register #(.width(32)) register_12 (
    .D(write_data), .en(demultiplexer_1_out11), .clk(clock), .Q(register_12_q));  // open: clr
  Register #(.width(32)) register_13 (
    .D(write_data), .en(demultiplexer_1_out12), .clk(clock), .Q(register_13_q));  // open: clr
  Register #(.width(32)) register_14 (
    .D(write_data), .en(demultiplexer_1_out13), .clk(clock), .Q(register_14_q));  // open: clr
  Register #(.width(32)) register_15 (
    .D(write_data), .en(demultiplexer_1_out14), .clk(clock), .Q(register_15_q));  // open: clr
  Register #(.width(32)) register_16 (
    .D(write_data), .en(demultiplexer_1_out15), .clk(clock), .Q(register_16_q));  // open: clr
  Register #(.width(32)) register_17 (
    .D(write_data), .en(demultiplexer_1_out16), .clk(clock), .Q(register_17_q));  // open: clr
  Register #(.width(32)) register_18 (
    .D(write_data), .en(demultiplexer_1_out17), .clk(clock), .Q(register_18_q));  // open: clr
  Register #(.width(32)) register_19 (
    .D(write_data), .en(demultiplexer_1_out18), .clk(clock), .Q(register_19_q));  // open: clr
  Register #(.width(32)) register_20 (
    .D(write_data), .en(demultiplexer_1_out19), .clk(clock), .Q(register_20_q));  // open: clr
  Register #(.width(32)) register_21 (
    .D(write_data), .en(demultiplexer_1_out20), .clk(clock), .Q(register_21_q));  // open: clr
  Register #(.width(32)) register_22 (
    .D(write_data), .en(demultiplexer_1_out21), .clk(clock), .Q(register_22_q));  // open: clr
  Register #(.width(32)) register_23 (
    .D(write_data), .en(demultiplexer_1_out22), .clk(clock), .Q(register_23_q));  // open: clr
  Register #(.width(32)) register_24 (
    .D(write_data), .en(demultiplexer_1_out23), .clk(clock), .Q(register_24_q));  // open: clr
  Register #(.width(32)) register_25 (
    .D(write_data), .en(demultiplexer_1_out24), .clk(clock), .Q(register_25_q));  // open: clr
  Register #(.width(32)) register_26 (
    .D(write_data), .en(demultiplexer_1_out25), .clk(clock), .Q(register_26_q));  // open: clr
  Register #(.width(32)) register_27 (
    .D(write_data), .en(demultiplexer_1_out26), .clk(clock), .Q(register_27_q));  // open: clr
  Register #(.width(32)) register_28 (
    .D(write_data), .en(demultiplexer_1_out27), .clk(clock), .Q(register_28_q));  // open: clr
  Register #(.width(32)) register_29 (
    .D(write_data), .en(demultiplexer_1_out28), .clk(clock), .Q(register_29_q));  // open: clr
  Register #(.width(32)) register_30 (
    .D(write_data), .en(demultiplexer_1_out29), .clk(clock), .Q(register_30_q));  // open: clr
  Register #(.width(32)) register_31 (
    .D(write_data), .en(demultiplexer_1_out30), .clk(clock), .Q(register_31_q));  // open: clr
  Register #(.width(32)) register_32 (
    .D(write_data), .en(demultiplexer_1_out31), .clk(clock), .Q(register_32_q));  // open: clr
  Multiplexer #(.select(5), .width(32)) multiplexer_1 (
    .in0(register_1_q), .in1(register_2_q), .in2(register_3_q), .in3(register_4_q), .in4(register_5_q),
    .in5(register_6_q), .in6(register_7_q), .in7(register_8_q), .in8(register_9_q), .in9(register_10_q),
    .in10(register_11_q), .in11(register_12_q), .in12(register_13_q), .in13(register_14_q),
    .in14(register_15_q), .in15(register_16_q), .in16(register_17_q), .in17(register_18_q),
    .in18(register_19_q), .in19(register_20_q), .in20(register_21_q), .in21(register_22_q),
    .in22(register_23_q), .in23(register_24_q), .in24(register_25_q), .in25(register_26_q),
    .in26(register_27_q), .in27(register_28_q), .in28(register_29_q), .in29(register_30_q),
    .in30(register_31_q), .in31(register_32_q), .out(read_data_1), .sel(read_rg_1));
  Multiplexer #(.select(5), .width(32)) multiplexer_2 (
    .in0(register_1_q), .in1(register_2_q), .in2(register_3_q), .in3(register_4_q), .in4(register_5_q),
    .in5(register_6_q), .in6(register_7_q), .in7(register_8_q), .in8(register_9_q), .in9(register_10_q),
    .in10(register_11_q), .in11(register_12_q), .in12(register_13_q), .in13(register_14_q),
    .in14(register_15_q), .in15(register_16_q), .in16(register_17_q), .in17(register_18_q),
    .in18(register_19_q), .in19(register_20_q), .in20(register_21_q), .in21(register_22_q),
    .in22(register_23_q), .in23(register_24_q), .in24(register_25_q), .in25(register_26_q),
    .in26(register_27_q), .in27(register_28_q), .in28(register_29_q), .in29(register_30_q),
    .in30(register_31_q), .in31(register_32_q), .out(read_data_2), .sel(read_rg_2));
endmodule

module ALU_control (
  input  [1:0] alu_op_in,
  input  [5:0] in_2,
  output [3:0] out_3
);

  wire an6_out, and_1_out, and_2_out, and_4_out, and_5_out, R_out, slt_out, sub_out;

  and R (R_out, ~alu_op_in[0], alu_op_in[1]);  // AND_Gate
  // AND_Gate add has open pins: in0=in_2[0], in1=in_2[1], in2=in_2[2], in3=in_2[3], in4=in_2[4], in5=in_2[5], out=open
  and sub (sub_out, ~in_2[0], in_2[1], ~in_2[2], ~in_2[3], ~in_2[4], in_2[5]);  // AND_Gate
  and an6 (an6_out, ~in_2[0], ~in_2[1], in_2[2], ~in_2[3], ~in_2[4], in_2[5]);  // AND_Gate
  and slt (slt_out, ~in_2[0], in_2[1], ~in_2[2], in_2[3], ~in_2[4], in_2[5]);  // AND_Gate
  and and_1 (and_1_out, R_out, slt_out);
  and and_2 (and_2_out, alu_op_in[0], ~alu_op_in[1]);  // AND_Gate
  and and_3 (out_3[0], slt_out, R_out);
  not not_1 (out_3[1], and_4_out);
  and and_4 (and_4_out, an6_out, R_out);
  and and_5 (and_5_out, R_out, sub_out);
  or or_1 (out_3[2], and_1_out, and_5_out, and_2_out);

  assign out_3[3] = 1'b0;
endmodule

module control (
  input  [5:0] opcode,
  output [1:0] alu_op,
  output reg_dst,
  output reg_write,
  output mem_read,
  output ALU_src,
  output memto_reg,
  output mem_write,
  output PC_src,
  output branch
);

  and R (alu_op[1], ~opcode[0], ~opcode[1], ~opcode[2], ~opcode[3], ~opcode[4], ~opcode[5]);  // AND_Gate
  and lw (mem_read, ~opcode[0], ~opcode[1], opcode[2], opcode[3], ~opcode[4], ~opcode[5]);  // AND_Gate
  and sw (mem_write, opcode[0], opcode[1], ~opcode[2], opcode[3], ~opcode[4], opcode[5]);  // AND_Gate
  and beq (alu_op[0], ~opcode[0], ~opcode[1], ~opcode[2], opcode[3], ~opcode[4], ~opcode[5]);  // AND_Gate
  or or_1 (reg_write, alu_op[1], mem_read);
  or or_2 (ALU_src, mem_read, mem_write);

  assign branch = alu_op[0];
  assign memto_reg = mem_read;
  assign PC_src = alu_op[0];
  assign reg_dst = alu_op[1];
endmodule
